# Fritzing sketch schema (saved by Fritzing 1.0.5)

parts:
  M1 = advancer muscle sensor v3
  Mod1 = Amica NodeMCU DEVKIT 1.0
  SEN1 = Pulse Sensor [package=SIP-3]  # not connected
  VCC3 = Battery [internal_resistance=0.1Ω]
  VCC4 = Battery [internal_resistance=0.1Ω]
  IC2 = AD8232 HeartRate Monitor [part_number=SEN-12650 chip_label=IC package="DIP (Dual Inline) [THT]"]
  Mod2 = Amica NodeMCU DEVKIT 1.0  # not connected

nets:
  N1: M1.+Vs, VCC3.+
  GND: M1.GND, Mod1.pin2, Mod1.pin_25, Mod1.pin_29, VCC3.-, IC2.GND
  N2: M1.-Vs, VCC4.-
  N3: M1.SIG, Mod1.pin_14
  N4: Mod1.pin_26, IC2.3.3v

notes:
  garmin watch

custom parts:
  advancer muscle sensor v3: This sensor will measure the filtered and rectified electrical activity of a muscle; outputting 0-Vs Volts depending the amount of activity in the selected muscle, where Vs signifies the voltage of the power source. Power supply voltage: min. +-3.5V.
  Pulse Sensor: Pulse Sensor Optical Heart Beat Sensor
  AD8232 HeartRate Monitor: A DIP stand-in part for whatever IC you want. With 10 pins on a 600mil dual inline package (DIP) footprint.
